// Logisim project 8-bit_cpu1.circ as structural Verilog: 2 circuits, main circuit main
module main (
);

  _74161 #(.ShowInternalStructure("true"), .VccGndPorts("true")) u_74161_1 ();  // open: pin1, pin2, pin3, pin4, pin5, pin6, pin7, pin8, pin16, pin15, pin14, pin13, pin12, pin11, pin10, pin9
  _74283 #(.ShowInternalStructure("true"), .VccGndPorts("true")) u_74283_1 ();  // open: pin1, pin2, pin3, pin4, pin5, pin6, pin7, pin8, pin16, pin15, pin14, pin13, pin12, pin11, pin10, pin9
  _7486 #(.ShowInternalStructure("true"), .VccGndPorts("true")) u_7486_1 ();  // open: pin1, pin2, pin3, pin4, pin5, pin6, pin7, pin14, pin13, pin12, pin11, pin10, pin9, pin8
  _74245 #(.ShowInternalStructure("true"), .VccGndPorts("true")) u_74245_1 ();  // open: pin1, pin2, pin3, pin4, pin5, pin6, pin7, pin8, pin9, pin10, pin20, pin19, pin18, pin17, pin16, pin15, pin14, pin13, pin12, pin11
  _74377 #(.ShowInternalStructure("true")) u_74377_1 ();  // open: pin1, pin2, pin3, pin4, pin5, pin6, pin7, pin8, pin9, pin19, pin18, pin17, pin16, pin15, pin14, pin13, pin12, pin11
  _74157 #(.ShowInternalStructure("true"), .VccGndPorts("true")) u_74157_1 ();  // open: pin1, pin2, pin3, pin4, pin5, pin6, pin7, pin8, pin16, pin15, pin14, pin13, pin12, pin11, pin10, pin9

  // Notes on the sheet:
  //   HC
  //   no
  //   yes
  //   no
  //   yes
  //   no
  //   yes
  //   no
  //   yes
  //   no
  //   yes
  //   yes
  //   yes
endmodule

module CPU (
  input  Program_Mode
);

  wire ALO, ARI, ARO, BRI, button_1_out, CF, CLK, dipswitch_1_p1, dipswitch_1_p2, dipswitch_1_p3,
       dipswitch_1_p4, dipswitch_1_p5, dipswitch_1_p6, dipswitch_1_p7, dipswitch_1_p8, dipswitch_2_p1,
       dipswitch_2_p2, dipswitch_2_p3, dipswitch_2_p4, HLT, IRI, IRO, JMP, MRI, n7404_1_pin11, n7404_1_pin12,
       n7408_1_pin1, n7408_2_pin3, n7408_2_pin6, n7436_1_pin3, n7436_1_pin6, n7436_1_pin8, n7436_1_pin11,
       n7486_1_pin3, n7486_1_pin6, n7486_1_pin8, n7486_1_pin11, n7486_2_pin3, n7486_2_pin6, n7486_2_pin8,
       n7486_2_pin11, n74138_1_pin4, n74138_1_pin6, n74138_2_pin4, n74138_2_pin6, n74157_1_pin9,
       n74157_1_pin12, n74157_1_pin13, n74157_1_pin15, n74157_2_pin2, n74157_2_pin5, n74157_2_pin11,
       n74157_2_pin14, n74157_2_pin15, n74157_3_pin2, n74157_3_pin5, n74157_3_pin11, n74157_3_pin14,
       n74157_4_pin2, n74157_4_pin5, n74157_4_pin11, n74157_4_pin14, n74157_4_pin15, n74161_1_pin7,
       n74161_1_pin10, n74161_2_pin1, n74161_2_pin10, n74161_2_pin11, n74161_2_pin12, n74161_2_pin13,
       n74161_2_pin14, n74245_2_pin1, n74245_2_pin14, n74245_2_pin15, n74245_2_pin16, n74245_2_pin17,
       n74245_2_pin18, n74245_3_pin1, n74245_3_pin18, n74245_4_pin1, n74245_5_pin1, n74283_1_pin1,
       n74283_1_pin4, n74283_1_pin9, n74283_1_pin10, n74283_1_pin13, n74283_2_pin1, n74283_2_pin4,
       n74283_2_pin9, n74283_2_pin10, n74283_2_pin13, n74377_1_pin3, n74377_1_pin7, n74377_3_pin2,
       n74377_3_pin5, n74377_3_pin6, n74377_3_pin9, n74377_3_pin12, n74377_3_pin15, n74377_3_pin16,
       n74377_3_pin19, n74377_4_pin2, n74377_4_pin5, n74377_4_pin6, n74377_4_pin9, n74377_4_pin12,
       n74377_4_pin15, n74377_4_pin16, n74377_4_pin19, n74377_6_pin4, n74377_6_pin7, n74377_6_pin18, ORI,
       PCE, PCO, RAI, RAO, SKP, SUB, ZF;
  wire [3:0] n74157_4_pin12;
  wire [5:0] rom_1_data;
  wire [6:0] n74161_1_pin14;
  wire [7:0] n74157_2_pin4, n74377_5_pin2, ram_1_dout;

  Button button_1 (.out(button_1_out));
  // DipSwitch dipswitch_1: pin names not known; wires that end beside it: dipswitch_1_p1, dipswitch_1_p2, dipswitch_1_p3, dipswitch_1_p4, dipswitch_1_p5, dipswitch_1_p6, dipswitch_1_p7, dipswitch_1_p8
  _74157 #(.ShowInternalStructure("true")) u_74157_1 (
    .pin1(Program_Mode), .pin15(n74157_1_pin15), .pin14(RAI), .pin13(n74157_1_pin13), .pin12(n74157_1_pin12),
    .pin11(CLK), .pin10(button_1_out), .pin9(n74157_1_pin9));  // open: pin2, pin3, pin4, pin5, pin6, pin7
  // DipSwitch #(.number(4)) dipswitch_2: pin names not known; wires that end beside it: dipswitch_2_p1, dipswitch_2_p2, dipswitch_2_p3, dipswitch_2_p4
  _74157 #(.ShowInternalStructure("true")) u_74157_2 (
    .pin1(Program_Mode), .pin2(n74157_2_pin2), .pin3(dipswitch_1_p8), .pin4(n74157_2_pin4[0]),
    .pin5(n74157_2_pin5), .pin6(dipswitch_1_p7), .pin7(n74157_2_pin4[1]), .pin15(n74157_2_pin15),
    .pin14(n74157_2_pin14), .pin13(dipswitch_1_p5), .pin12(n74157_2_pin4[3]), .pin11(n74157_2_pin11),
    .pin10(dipswitch_1_p6), .pin9(n74157_2_pin4[2]));
  _74157 #(.ShowInternalStructure("true")) u_74157_3 (
    .pin1(Program_Mode), .pin2(n74157_3_pin2), .pin3(dipswitch_1_p4), .pin4(n74157_2_pin4[4]),
    .pin5(n74157_3_pin5), .pin6(dipswitch_1_p3), .pin7(n74157_2_pin4[5]), .pin14(n74157_3_pin14),
    .pin13(dipswitch_1_p1), .pin12(n74157_2_pin4[7]), .pin11(n74157_3_pin11), .pin10(dipswitch_1_p2),
    .pin9(n74157_2_pin4[6]));  // open: pin15
  RAM #(.addrWidth(4), .enables("line")) ram_1 (
    .addr(n74157_4_pin12), .we(n74157_1_pin12), .clk(n74157_1_pin9), .din(n74157_2_pin4), .dout(ram_1_dout));
  _7404 #(.ShowInternalStructure("true")) u_7404_1 (
    .pin13(CLK), .pin12(n7404_1_pin12), .pin11(n7404_1_pin11), .pin10(RAI));  // open: pin1, pin2, pin3, pin4, pin5, pin6, pin9, pin8
  _74157 #(.ShowInternalStructure("true")) u_74157_4 (
    .pin1(Program_Mode), .pin2(n74157_4_pin2), .pin3(dipswitch_2_p2), .pin4(n74157_4_pin12[2]),
    .pin5(n74157_4_pin5), .pin6(dipswitch_2_p1), .pin7(n74157_4_pin12[3]), .pin15(n74157_4_pin15),
    .pin14(n74157_4_pin14), .pin13(dipswitch_2_p4), .pin12(n74157_4_pin12[0]), .pin11(n74157_4_pin11),
    .pin10(dipswitch_2_p3), .pin9(n74157_4_pin12[1]));
  _74161 #(.ShowInternalStructure("true")) u_74161_1 (
    .pin1(SKP), .pin2(n7404_1_pin12), .pin7(n74161_1_pin7), .pin14(n74161_1_pin14[0]),
    .pin13(n74161_1_pin14[1]), .pin12(n74161_1_pin14[2]), .pin10(n74161_1_pin10));  // open: pin3, pin4, pin5, pin6, pin15, pin11, pin9
  _74245 #(.ShowInternalStructure("true")) u_74245_1 (
    .pin2(n74157_3_pin14), .pin3(n74157_3_pin11), .pin4(n74157_3_pin5), .pin5(n74157_3_pin2),
    .pin6(n74157_2_pin14), .pin7(n74157_2_pin11), .pin8(n74157_2_pin5), .pin9(n74157_2_pin2), .pin19(RAO),
    .pin18(ram_1_dout[7]), .pin17(ram_1_dout[6]), .pin16(ram_1_dout[5]), .pin15(ram_1_dout[4]),
    .pin14(ram_1_dout[3]), .pin13(ram_1_dout[2]), .pin12(ram_1_dout[1]), .pin11(ram_1_dout[0]));  // open: pin1
  ROM #(.addrWidth(9)) rom_1 (.addr({ZF, CF, n74161_1_pin14}), .data({SUB, PCE, rom_1_data}));
  _7408 #(.ShowInternalStructure("true")) u_7408_1 (
    .pin1(n7408_1_pin1), .pin2(HLT), .pin3(CLK));  // open: pin4, pin5, pin6, pin13, pin12, pin11, pin10, pin9, pin8
  Clock clock_1 (.out(n7408_1_pin1));
  Pull_Resistor pull_resistor_1 (.node(n74157_3_pin14));
  Pull_Resistor pull_resistor_2 (.node(n74157_3_pin11));
  Pull_Resistor pull_resistor_3 (.node(n74157_3_pin5));
  Pull_Resistor pull_resistor_4 (.node(n74157_3_pin2));
  // Probe on n74157_3_pin14
  // Probe on n74157_3_pin5
  _74377 #(.ShowInternalStructure("true")) u_74377_1 (
    .pin1(MRI), .pin3(n74377_1_pin3), .pin4(n74377_1_pin3), .pin7(n74377_1_pin7), .pin8(n74377_1_pin7),
    .pin19(n74157_4_pin5), .pin18(n74157_2_pin14), .pin17(n74157_2_pin11), .pin16(n74157_4_pin2),
    .pin15(n74157_4_pin11), .pin14(n74157_2_pin5), .pin13(n74157_2_pin2), .pin12(n74157_4_pin14), .pin11(CLK));  // open: pin2, pin5, pin6, pin9
  // Probe on n74157_3_pin11
  // Probe on n74157_3_pin2
  _74245 #(.ShowInternalStructure("true")) u_74245_2 (
    .pin1(n74245_2_pin1), .pin2(n74157_2_pin2), .pin3(n74157_2_pin5), .pin4(n74157_2_pin11),
    .pin5(n74157_2_pin14), .pin6(n74157_3_pin2), .pin7(n74157_3_pin5), .pin8(n74157_3_pin11),
    .pin9(n74157_3_pin14), .pin19(IRO), .pin18(n74245_2_pin18), .pin17(n74245_2_pin17),
    .pin16(n74245_2_pin16), .pin15(n74245_2_pin15), .pin14(n74245_2_pin14), .pin13(n74245_2_pin14),
    .pin12(n74245_2_pin14), .pin11(n74245_2_pin14));
  _74377 #(.ShowInternalStructure("true")) u_74377_2 (
    .pin1(IRI), .pin2(n74245_2_pin18), .pin3(n74157_2_pin2), .pin4(n74157_2_pin5), .pin5(n74245_2_pin17),
    .pin6(n74245_2_pin16), .pin7(n74157_2_pin11), .pin8(n74157_2_pin14), .pin9(n74245_2_pin15),
    .pin19(n74161_1_pin14[6]), .pin18(n74157_3_pin14), .pin17(n74157_3_pin11), .pin16(n74161_1_pin14[5]),
    .pin15(n74161_1_pin14[4]), .pin14(n74157_3_pin5), .pin13(n74157_3_pin2), .pin12(n74161_1_pin14[3]),
    .pin11(CLK));
  Pull_Resistor pull_resistor_5 (.node(n74157_2_pin14));
  Pull_Resistor pull_resistor_6 (.node(n74157_2_pin11));
  Pull_Resistor pull_resistor_7 (.node(n74157_2_pin5));
  Pull_Resistor pull_resistor_8 (.node(n74157_2_pin2));
  _74161 #(.ShowInternalStructure("true")) u_74161_2 (
    .pin1(n74161_2_pin1), .pin2(CLK), .pin3(n74157_2_pin2), .pin4(n74157_2_pin5), .pin5(n74157_2_pin11),
    .pin6(n74157_2_pin14), .pin7(PCE), .pin14(n74161_2_pin14), .pin13(n74161_2_pin13),
    .pin12(n74161_2_pin12), .pin11(n74161_2_pin11), .pin10(n74161_2_pin10), .pin9(JMP));  // open: pin15
  // Probe on n74157_2_pin14
  // Probe on n74157_2_pin5
  // Probe on n74157_2_pin11
  // Probe on n74157_2_pin2
  _74377 #(.ShowInternalStructure("true")) u_74377_3 (
    .pin1(ARI), .pin2(n74377_3_pin2), .pin3(n74157_2_pin2), .pin4(n74157_2_pin5), .pin5(n74377_3_pin5),
    .pin6(n74377_3_pin6), .pin7(n74157_2_pin11), .pin8(n74157_2_pin14), .pin9(n74377_3_pin9),
    .pin19(n74377_3_pin19), .pin18(n74157_3_pin14), .pin17(n74157_3_pin11), .pin16(n74377_3_pin16),
    .pin15(n74377_3_pin15), .pin14(n74157_3_pin5), .pin13(n74157_3_pin2), .pin12(n74377_3_pin12), .pin11(CLK));
  _74377 #(.ShowInternalStructure("true")) u_74377_4 (
    .pin1(BRI), .pin2(n74377_4_pin2), .pin3(n74157_2_pin2), .pin4(n74157_2_pin5), .pin5(n74377_4_pin5),
    .pin6(n74377_4_pin6), .pin7(n74157_2_pin11), .pin8(n74157_2_pin14), .pin9(n74377_4_pin9),
    .pin19(n74377_4_pin19), .pin18(n74157_3_pin14), .pin17(n74157_3_pin14), .pin16(n74377_4_pin16),
    .pin15(n74377_4_pin15), .pin14(n74157_3_pin14), .pin13(n74157_3_pin14), .pin12(n74377_4_pin12),
    .pin11(CLK));
  _7486 #(.ShowInternalStructure("true")) u_7486_1 (
    .pin1(n74377_4_pin5), .pin2(SUB), .pin3(n7486_1_pin3), .pin4(n74377_4_pin9), .pin5(SUB),
    .pin6(n7486_1_pin6), .pin13(n74377_4_pin2), .pin12(SUB), .pin11(n7486_1_pin11), .pin10(n74377_4_pin6),
    .pin9(SUB), .pin8(n7486_1_pin8));
  _74138 #(.ShowInternalStructure("true")) u_74138_1 (
    .pin1(rom_1_data[0]), .pin2(rom_1_data[1]), .pin3(rom_1_data[2]), .pin4(n74138_1_pin4),
    .pin5(n74138_1_pin4), .pin6(n74138_1_pin6), .pin7(HLT), .pin14(PCO), .pin13(IRO), .pin12(RAO),
    .pin11(ARO), .pin10(SKP), .pin9(ALO));  // open: pin15
  _74245 #(.ShowInternalStructure("true")) u_74245_3 (
    .pin1(n74245_3_pin1), .pin2(n74157_3_pin14), .pin3(n74157_3_pin11), .pin4(n74157_3_pin5),
    .pin5(n74157_3_pin2), .pin6(n74157_2_pin14), .pin7(n74157_2_pin11), .pin8(n74157_2_pin5),
    .pin9(n74157_2_pin2), .pin19(PCO), .pin18(n74245_3_pin18), .pin17(n74245_3_pin18),
    .pin16(n74245_3_pin18), .pin15(n74245_3_pin18), .pin14(n74161_2_pin11), .pin13(n74161_2_pin12),
    .pin12(n74161_2_pin13), .pin11(n74161_2_pin14));
  _7486 #(.ShowInternalStructure("true")) u_7486_2 (
    .pin1(n74377_4_pin15), .pin2(SUB), .pin3(n7486_2_pin3), .pin4(n74377_4_pin19), .pin5(SUB),
    .pin6(n7486_2_pin6), .pin13(n74377_4_pin12), .pin12(SUB), .pin11(n7486_2_pin11), .pin10(n74377_4_pin16),
    .pin9(SUB), .pin8(n7486_2_pin8));
  _74138 #(.ShowInternalStructure("true")) u_74138_2 (
    .pin1(rom_1_data[3]), .pin2(rom_1_data[4]), .pin3(rom_1_data[5]), .pin4(n74138_2_pin4),
    .pin5(n74138_2_pin4), .pin6(n74138_2_pin6), .pin7(ORI), .pin14(JMP), .pin13(IRI), .pin12(n7404_1_pin11),
    .pin11(ARI), .pin10(BRI), .pin9(MRI));  // open: pin15
  _74377 #(.ShowInternalStructure("true")) u_74377_5 (
    .pin1(ORI), .pin2(n74377_5_pin2[0]), .pin3(n74157_2_pin2), .pin4(n74157_2_pin5), .pin5(n74377_5_pin2[1]),
    .pin6(n74377_5_pin2[2]), .pin7(n74157_2_pin11), .pin8(n74157_2_pin14), .pin9(n74377_5_pin2[3]),
    .pin19(n74377_5_pin2[7]), .pin18(n74157_3_pin14), .pin17(n74157_3_pin11), .pin16(n74377_5_pin2[6]),
    .pin15(n74377_5_pin2[5]), .pin14(n74157_3_pin5), .pin13(n74157_3_pin2), .pin12(n74377_5_pin2[4]),
    .pin11(CLK));
  _74245 #(.ShowInternalStructure("true")) u_74245_4 (
    .pin1(n74245_4_pin1), .pin2(n74157_2_pin2), .pin3(n74157_2_pin5), .pin4(n74157_2_pin11),
    .pin5(n74157_2_pin14), .pin6(n74157_3_pin2), .pin7(n74157_3_pin5), .pin8(n74157_3_pin11),
    .pin9(n74157_3_pin14), .pin19(ARO), .pin18(n74377_3_pin2), .pin17(n74377_3_pin5), .pin16(n74377_3_pin6),
    .pin15(n74377_3_pin9), .pin14(n74377_3_pin12), .pin13(n74377_3_pin15), .pin12(n74377_3_pin16),
    .pin11(n74377_3_pin19));
  _74283 #(.ShowInternalStructure("true")) u_74283_1 (
    .pin1(n74283_1_pin1), .pin2(n7486_1_pin3), .pin3(n74377_3_pin5), .pin4(n74283_1_pin4),
    .pin5(n74377_3_pin2), .pin6(n7486_1_pin11), .pin7(SUB), .pin15(n7486_1_pin8), .pin14(n74377_3_pin6),
    .pin13(n74283_1_pin13), .pin12(n74377_3_pin9), .pin11(n7486_1_pin6), .pin10(n74283_1_pin10),
    .pin9(n74283_1_pin9));
  _74283 #(.ShowInternalStructure("true")) u_74283_2 (
    .pin1(n74283_2_pin1), .pin2(n7486_2_pin3), .pin3(n74377_3_pin15), .pin4(n74283_2_pin4),
    .pin5(n74377_3_pin12), .pin6(n7486_2_pin11), .pin7(n74283_1_pin9), .pin15(n7486_2_pin8),
    .pin14(n74377_3_pin16), .pin13(n74283_2_pin13), .pin12(n74377_3_pin19), .pin11(n7486_2_pin6),
    .pin10(n74283_2_pin10), .pin9(n74283_2_pin9));
  _7436 #(.ShowInternalStructure("true")) u_7436_1 (
    .pin1(n74283_2_pin10), .pin2(n74283_2_pin13), .pin3(n7436_1_pin3), .pin4(n74283_2_pin1),
    .pin5(n74283_2_pin4), .pin6(n7436_1_pin6), .pin13(n74283_1_pin13), .pin12(n74283_1_pin10),
    .pin11(n7436_1_pin11), .pin10(n74283_1_pin1), .pin9(n74283_1_pin4), .pin8(n7436_1_pin8));
  _74377 #(.ShowInternalStructure("true")) u_74377_6 (
    .pin1(ALO), .pin2(CF), .pin3(n74283_2_pin9), .pin4(n74377_6_pin4), .pin5(ZF), .pin7(n74377_6_pin7),
    .pin8(n74377_6_pin7), .pin18(n74377_6_pin18), .pin17(n74377_6_pin18), .pin14(n74377_6_pin18),
    .pin13(n74377_6_pin18), .pin11(CLK));  // open: pin6, pin9, pin19, pin16, pin15, pin12
  _7_Segment_Display u_7_segment_display_1 ();  // open: g, f, a, b, e, d, c, dp
  _7_Segment_Display u_7_segment_display_2 ();  // open: g, f, a, b, e, d, c, dp
  // BCD_to_7_Segment_decoder bcd_to_7_segment_decoder_1: pin names not known
  // BCD_to_7_Segment_decoder bcd_to_7_segment_decoder_2: pin names not known
  // Binary_to_BCD_converter #(.binvalue(8)) binary_to_bcd_converter_1: pin names not known
  _7_Segment_Display u_7_segment_display_3 ();  // open: g, f, a, b, e, d, c, dp
  // BCD_to_7_Segment_decoder bcd_to_7_segment_decoder_3: pin names not known; wires that end beside it: n74157_2_pin2, n74157_2_pin5, n74157_2_pin11, n74157_2_pin14, n74157_3_pin2, n74157_3_pin5, n74157_3_pin11, n74157_3_pin14
  _74245 #(.ShowInternalStructure("true")) u_74245_5 (
    .pin1(n74245_5_pin1), .pin2(n74157_2_pin2), .pin3(n74157_2_pin5), .pin4(n74157_2_pin11),
    .pin5(n74157_2_pin14), .pin6(n74157_3_pin2), .pin7(n74157_3_pin5), .pin8(n74157_3_pin11),
    .pin9(n74157_3_pin14), .pin19(ALO), .pin18(n74283_1_pin4), .pin17(n74283_1_pin1), .pin16(n74283_1_pin13),
    .pin15(n74283_1_pin10), .pin14(n74283_2_pin4), .pin13(n74283_2_pin1), .pin12(n74283_2_pin13),
    .pin11(n74283_2_pin10));
  _7408 #(.ShowInternalStructure("true")) u_7408_2 (
    .pin1(n7436_1_pin3), .pin2(n7436_1_pin6), .pin3(n7408_2_pin3), .pin4(n7436_1_pin11), .pin5(n7436_1_pin8),
    .pin6(n7408_2_pin6), .pin13(n7408_2_pin3), .pin12(n7408_2_pin6), .pin11(n74377_6_pin4));  // open: pin10, pin9, pin8
  // also tied to GND on the sheet: {n74157_1_pin15, n74157_2_pin15, n74157_4_pin15, n74245_2_pin14, n74377_1_pin7, n74377_1_pin3, n74245_2_pin1, n74245_3_pin1, n74138_1_pin4, n74245_3_pin18, n74138_2_pin4, n74245_4_pin1, n74377_6_pin18, n74377_6_pin7, n74245_5_pin1}
  // also tied to VCC on the sheet: {n74157_1_pin13, n74161_1_pin7, n74161_1_pin10, n74161_2_pin1, n74161_2_pin10, n74138_1_pin6, n74138_2_pin6}

  // Other names for the same wires on the sheet: FRI = ALO; PM = Program_Mode

  // Notes on the sheet:
  //   RAM
  //   Instruction Register
  //   Memory Register
  //   contents of rom_1 (hex, n*v repeats v):
  //   31 53 6*5 31 53 32 23 4*5 31 53 32 2b 26 5 5 5 31 53 32 2b a6 5 5 5 31 53 32 1c 4*5 31 53 22 5*5 31
  //   53 a 5*5 31 53 6*5 31 53 6*5 31 53 2a 26 4*5 31 53 2a a6 4*5 31 53 6*5 31 53 6*5 31 53 6*5 31 53 3c
  //   5*5 31 53 7 5*5 31 53 6*5 31 53 32 23 4*5 31 53 32 2b 26 5 5 5 31 53 32 2b a6 5 5 5 31 53 32 1c 4*5
  //   31 53 22 5*5 31 53 a 5*5 31 53 a 5*5 31 53 6*5 31 53 2a 26 4*5 31 53 2a a6 4*5 31 53 6*5 31 53 6*5
  //   31 53 6*5 31 53 3c 5*5 31 53 7 5*5 31 53 6*5 31 53 32 23 4*5 31 53 32 2b 26 5 5 5 31 53 32 2b a6 5 5
  //   5 31 53 32 1c 4*5 31 53 22 5*5 31 53 a 5*5 31 53 6*5 31 53 a 5*5 31 53 2a 26 4*5 31 53 2a a6 4*5 31
  //   53 6*5 31 53 6*5 31 53 6*5 31 53 3c 5*5 31 53 7 5*5 31 53 6*5 31 53 32 23 4*5 31 53 32 2b 26 5 5 5
  //   31 53 32 2b a6 5 5 5 31 53 32 1c 4*5 31 53 22 5*5 31 53 a 5*5 31 53 a 5*5 31 53 a 5*5 31 53 2a 26
  //   4*5 31 53 2a a6 4*5 31 53 6*5 31 53 6*5 31 53 6*5 31 53 3c 5*5 31 53 7 5*5
  //   B Register
  //   A Register
  //   Decoder
  //   ALU
  //   Output-Register
endmodule
