// Logisim project 8-bit_cpu2.circ as structural Verilog: 2 circuits, main circuit main
module main (
);

  _74161 #(.ShowInternalStructure("true"), .VccGndPorts("true")) u_74161_1 ();  // open: pin1, pin2, pin3, pin4, pin5, pin6, pin7, pin8, pin16, pin15, pin14, pin13, pin12, pin11, pin10, pin9
  _74283 #(.ShowInternalStructure("true"), .VccGndPorts("true")) u_74283_1 ();  // open: pin1, pin2, pin3, pin4, pin5, pin6, pin7, pin8, pin16, pin15, pin14, pin13, pin12, pin11, pin10, pin9
  _7486 #(.ShowInternalStructure("true"), .VccGndPorts("true")) u_7486_1 ();  // open: pin1, pin2, pin3, pin4, pin5, pin6, pin7, pin14, pin13, pin12, pin11, pin10, pin9, pin8
  _74245 #(.ShowInternalStructure("true"), .VccGndPorts("true")) u_74245_1 ();  // open: pin1, pin2, pin3, pin4, pin5, pin6, pin7, pin8, pin9, pin10, pin20, pin19, pin18, pin17, pin16, pin15, pin14, pin13, pin12, pin11
  _74377 #(.ShowInternalStructure("true")) u_74377_1 ();  // open: pin1, pin2, pin3, pin4, pin5, pin6, pin7, pin8, pin9, pin19, pin18, pin17, pin16, pin15, pin14, pin13, pin12, pin11
  _74157 #(.ShowInternalStructure("true"), .VccGndPorts("true")) u_74157_1 ();  // open: pin1, pin2, pin3, pin4, pin5, pin6, pin7, pin8, pin16, pin15, pin14, pin13, pin12, pin11, pin10, pin9

  // Notes on the sheet:
  //   HC
  //   no
  //   yes
  //   no
  //   yes
  //   no
  //   yes
  //   no
  //   yes
  //   no
  //   yes
  //   yes
  //   yes
endmodule

module CPU (
);

  wire ALO, ARI, ARO, BRI, CF, CLK, HLT, IRI, IRO, JMP, MRI, n7404_1_pin2, n7408_1_pin1, n7408_2_pin4,
       n7408_2_pin5, n7436_1_pin3, n7436_1_pin6, n7436_1_pin8, n7436_1_pin11, n7486_1_pin3, n7486_1_pin6,
       n7486_1_pin8, n7486_1_pin11, n7486_2_pin3, n7486_2_pin6, n7486_2_pin8, n7486_2_pin11, n74138_1_pin4,
       n74138_1_pin6, n74138_2_pin4, n74138_2_pin6, n74138_2_pin12, n74161_1_pin1, n74161_1_pin3,
       n74161_1_pin4, n74161_1_pin5, n74161_1_pin6, n74161_1_pin11, n74161_2_pin1, n74161_2_pin3,
       n74161_2_pin4, n74161_2_pin5, n74161_2_pin6, n74161_2_pin10, n74161_3_pin2, n74161_3_pin3,
       n74161_3_pin7, n74161_3_pin10, n74161_4_pin1, n74161_4_pin10, n74161_4_pin11, n74161_4_pin12,
       n74161_4_pin13, n74161_4_pin14, n74161_5_pin1, n74161_5_pin10, n74161_5_pin11, n74161_5_pin12,
       n74161_5_pin13, n74161_5_pin14, n74245_3_pin1, n74245_4_pin1, n74245_5_pin1, n74283_1_pin1,
       n74283_1_pin4, n74283_1_pin9, n74283_1_pin10, n74283_1_pin13, n74283_2_pin1, n74283_2_pin4,
       n74283_2_pin9, n74283_2_pin10, n74283_2_pin13, n74377_2_pin2, n74377_2_pin5, n74377_2_pin6,
       n74377_2_pin9, n74377_2_pin12, n74377_2_pin15, n74377_2_pin16, n74377_2_pin19, n74377_3_pin2,
       n74377_3_pin5, n74377_3_pin6, n74377_3_pin9, n74377_3_pin12, n74377_3_pin15, n74377_3_pin16,
       n74377_3_pin19, n74377_5_pin4, n74377_5_pin7, n74377_5_pin18, ORI, PCE, PCO, RAI, RAO, SKP, SUB, ZF;
  wire [5:0] rom_2_data;
  wire [6:0] n74161_2_pin14;
  wire [7:0] n74161_3_pin14, n74377_4_pin2, ram_1_dout, rom_1_data;

  _74161 #(.ShowInternalStructure("true")) u_74161_1 (
    .pin1(n74161_1_pin1), .pin2(CLK), .pin3(n74161_1_pin3), .pin4(n74161_1_pin4), .pin5(n74161_1_pin5),
    .pin6(n74161_1_pin6), .pin7(PCE), .pin14(n74161_2_pin14[4]), .pin13(n74161_2_pin14[5]),
    .pin12(n74161_2_pin14[6]), .pin11(n74161_1_pin11), .pin9(MRI));  // open: pin15, pin10
  ROM #(.addrWidth(7)) rom_1 (.addr(n74161_2_pin14), .data(rom_1_data));
  RAM #(.addrWidth(7), .enables("line")) ram_1 (
    .addr(n74161_2_pin14), .we(RAI), .clk(CLK), .dout(ram_1_dout));  // open: din
  _7404 #(.ShowInternalStructure("true")) u_7404_1 (
    .pin1(n74161_1_pin11), .pin2(n7404_1_pin2));  // open: pin3, pin4, pin5, pin6, pin13, pin12, pin11, pin10, pin9, pin8
  _74161 #(.ShowInternalStructure("true")) u_74161_2 (
    .pin1(n74161_2_pin1), .pin2(CLK), .pin3(n74161_2_pin3), .pin4(n74161_2_pin4), .pin5(n74161_2_pin5),
    .pin6(n74161_2_pin6), .pin7(PCE), .pin14(n74161_2_pin14[0]), .pin13(n74161_2_pin14[1]),
    .pin12(n74161_2_pin14[2]), .pin11(n74161_2_pin14[3]), .pin10(n74161_2_pin10), .pin9(MRI));  // open: pin15
  _74377 #(.ShowInternalStructure("true")) u_74377_1 (
    .pin1(IRI), .pin2(n74161_3_pin14[3]), .pin3(n74161_2_pin3), .pin4(n74161_2_pin4),
    .pin5(n74161_3_pin14[4]), .pin6(n74161_3_pin14[5]), .pin7(n74161_2_pin5), .pin8(n74161_2_pin6),
    .pin9(n74161_3_pin14[6]), .pin18(n74161_1_pin6), .pin17(n74161_1_pin5), .pin14(n74161_1_pin4),
    .pin13(n74161_1_pin3), .pin12(n74161_3_pin14[7]), .pin11(CLK));  // open: pin19, pin16, pin15
  _74161 #(.ShowInternalStructure("true")) u_74161_3 (
    .pin1(SKP), .pin2(n74161_3_pin2), .pin3(n74161_3_pin3), .pin4(n74161_3_pin3), .pin5(n74161_3_pin3),
    .pin6(n74161_3_pin3), .pin7(n74161_3_pin7), .pin14(n74161_3_pin14[0]), .pin13(n74161_3_pin14[1]),
    .pin12(n74161_3_pin14[2]), .pin10(n74161_3_pin10), .pin9(n74161_3_pin10));  // open: pin15, pin11
  not not_1 (n74161_3_pin2, CLK);
  _7408 #(.ShowInternalStructure("true")) u_7408_1 (
    .pin1(n7408_1_pin1), .pin2(HLT), .pin3(CLK));  // open: pin4, pin5, pin6, pin13, pin12, pin11, pin10, pin9, pin8
  Clock clock_1 (.out(n7408_1_pin1));
  Pull_Resistor pull_resistor_1 (.node(n74161_1_pin6));
  Pull_Resistor pull_resistor_2 (.node(n74161_1_pin5));
  // Probe on n74161_1_pin6
  // Probe on n74161_1_pin5
  _74245 #(.ShowInternalStructure("true")) u_74245_1 (
    .pin1(n74161_1_pin11), .pin2(n74161_1_pin6), .pin3(n74161_1_pin5), .pin4(n74161_1_pin4),
    .pin5(n74161_1_pin3), .pin6(n74161_2_pin6), .pin7(n74161_2_pin5), .pin8(n74161_2_pin4),
    .pin9(n74161_2_pin3), .pin19(RAO), .pin18(rom_1_data[7]), .pin17(rom_1_data[6]), .pin16(rom_1_data[5]),
    .pin15(rom_1_data[4]), .pin14(rom_1_data[3]), .pin13(rom_1_data[2]), .pin12(rom_1_data[1]),
    .pin11(rom_1_data[0]));
  _74245 #(.ShowInternalStructure("true")) u_74245_2 (
    .pin1(n7404_1_pin2), .pin2(n74161_1_pin6), .pin3(n74161_1_pin5), .pin4(n74161_1_pin4),
    .pin5(n74161_1_pin3), .pin6(n74161_2_pin6), .pin7(n74161_2_pin5), .pin8(n74161_2_pin4),
    .pin9(n74161_2_pin3), .pin19(RAO), .pin18(ram_1_dout[7]), .pin17(ram_1_dout[6]), .pin16(ram_1_dout[5]),
    .pin15(ram_1_dout[4]), .pin14(ram_1_dout[3]), .pin13(ram_1_dout[2]), .pin12(ram_1_dout[1]),
    .pin11(ram_1_dout[0]));
  Pull_Resistor pull_resistor_3 (.node(n74161_1_pin4));
  Pull_Resistor pull_resistor_4 (.node(n74161_1_pin3));
  Pull_Resistor pull_resistor_5 (.node(n74161_2_pin6));
  Pull_Resistor pull_resistor_6 (.node(n74161_2_pin5));
  Pull_Resistor pull_resistor_7 (.node(n74161_2_pin4));
  Pull_Resistor pull_resistor_8 (.node(n74161_2_pin3));
  _74161 #(.ShowInternalStructure("true")) u_74161_4 (
    .pin1(n74161_4_pin1), .pin2(CLK), .pin3(n74161_1_pin3), .pin4(n74161_1_pin4), .pin5(n74161_1_pin5),
    .pin6(n74161_1_pin6), .pin7(PCE), .pin14(n74161_4_pin14), .pin13(n74161_4_pin13), .pin12(n74161_4_pin12),
    .pin11(n74161_4_pin11), .pin10(n74161_4_pin10), .pin9(JMP));  // open: pin15
  // Probe on n74161_1_pin4
  // Probe on n74161_2_pin6
  // Probe on n74161_2_pin4
  // Probe on n74161_1_pin3
  // Probe on n74161_2_pin5
  // Probe on n74161_2_pin3
  _74377 #(.ShowInternalStructure("true")) u_74377_2 (
    .pin1(ARI), .pin2(n74377_2_pin2), .pin3(n74161_2_pin3), .pin4(n74161_2_pin4), .pin5(n74377_2_pin5),
    .pin6(n74377_2_pin6), .pin7(n74161_2_pin5), .pin8(n74161_2_pin6), .pin9(n74377_2_pin9),
    .pin19(n74377_2_pin19), .pin18(n74161_1_pin6), .pin17(n74161_1_pin5), .pin16(n74377_2_pin16),
    .pin15(n74377_2_pin15), .pin14(n74161_1_pin4), .pin13(n74161_1_pin3), .pin12(n74377_2_pin12), .pin11(CLK));
  _74377 #(.ShowInternalStructure("true")) u_74377_3 (
    .pin1(BRI), .pin2(n74377_3_pin2), .pin3(n74161_2_pin3), .pin4(n74161_2_pin4), .pin5(n74377_3_pin5),
    .pin6(n74377_3_pin6), .pin7(n74161_2_pin5), .pin8(n74161_2_pin6), .pin9(n74377_3_pin9),
    .pin19(n74377_3_pin19), .pin18(n74161_1_pin6), .pin17(n74161_1_pin5), .pin16(n74377_3_pin16),
    .pin15(n74377_3_pin15), .pin14(n74161_1_pin4), .pin13(n74161_1_pin3), .pin12(n74377_3_pin12), .pin11(CLK));
  ROM #(.addrWidth(10)) rom_2 (.addr({ZF, CF, n74161_3_pin14}), .data({SUB, PCE, rom_2_data}));
  _74161 #(.ShowInternalStructure("true")) u_74161_5 (
    .pin1(n74161_5_pin1), .pin2(CLK), .pin3(n74161_2_pin3), .pin4(n74161_2_pin4), .pin5(n74161_2_pin5),
    .pin6(n74161_2_pin6), .pin7(PCE), .pin15(n74161_4_pin10), .pin14(n74161_5_pin14), .pin13(n74161_5_pin13),
    .pin12(n74161_5_pin12), .pin11(n74161_5_pin11), .pin10(n74161_5_pin10), .pin9(JMP));
  _74245 #(.ShowInternalStructure("true")) u_74245_3 (
    .pin1(n74245_3_pin1), .pin2(n74161_2_pin3), .pin3(n74161_2_pin4), .pin4(n74161_2_pin5),
    .pin5(n74161_2_pin6), .pin6(n74161_1_pin3), .pin7(n74161_1_pin4), .pin8(n74161_1_pin5),
    .pin9(n74161_1_pin6), .pin19(PCO), .pin18(n74161_5_pin14), .pin17(n74161_5_pin13),
    .pin16(n74161_5_pin12), .pin15(n74161_5_pin11), .pin14(n74161_4_pin14), .pin13(n74161_4_pin13),
    .pin12(n74161_4_pin12), .pin11(n74161_4_pin11));
  _7486 #(.ShowInternalStructure("true")) u_7486_1 (
    .pin1(n74377_3_pin16), .pin2(SUB), .pin3(n7486_1_pin3), .pin4(n74377_3_pin19), .pin5(SUB),
    .pin6(n7486_1_pin6), .pin13(n74377_3_pin12), .pin12(SUB), .pin11(n7486_1_pin11), .pin10(n74377_3_pin15),
    .pin9(SUB), .pin8(n7486_1_pin8));
  _7486 #(.ShowInternalStructure("true")) u_7486_2 (
    .pin1(n74377_3_pin6), .pin2(SUB), .pin3(n7486_2_pin3), .pin4(n74377_3_pin9), .pin5(SUB),
    .pin6(n7486_2_pin6), .pin13(n74377_3_pin2), .pin12(SUB), .pin11(n7486_2_pin11), .pin10(n74377_3_pin5),
    .pin9(SUB), .pin8(n7486_2_pin8));
  _74283 #(.ShowInternalStructure("true")) u_74283_1 (
    .pin1(n74283_1_pin1), .pin2(n7486_2_pin8), .pin3(n74377_2_pin5), .pin4(n74283_1_pin4),
    .pin5(n74377_2_pin2), .pin6(n7486_2_pin11), .pin7(SUB), .pin15(n7486_2_pin3), .pin14(n74377_2_pin6),
    .pin13(n74283_1_pin13), .pin12(n74377_2_pin9), .pin11(n7486_2_pin6), .pin10(n74283_1_pin10),
    .pin9(n74283_1_pin9));
  _74138 #(.ShowInternalStructure("true")) u_74138_1 (
    .pin1(rom_2_data[0]), .pin2(rom_2_data[1]), .pin3(rom_2_data[2]), .pin4(n74138_1_pin4),
    .pin5(n74138_1_pin4), .pin6(n74138_1_pin6), .pin7(HLT), .pin14(PCO), .pin13(IRO), .pin12(RAO),
    .pin11(ARO), .pin10(SKP), .pin9(ALO));  // open: pin15
  _74245 #(.ShowInternalStructure("true")) u_74245_4 (
    .pin1(n74245_4_pin1), .pin2(n74161_1_pin6), .pin3(n74161_1_pin5), .pin4(n74161_1_pin4),
    .pin5(n74161_1_pin3), .pin6(n74161_2_pin6), .pin7(n74161_2_pin5), .pin8(n74161_2_pin4),
    .pin9(n74161_2_pin3), .pin19(ARO), .pin18(n74377_2_pin19), .pin17(n74377_2_pin16),
    .pin16(n74377_2_pin15), .pin15(n74377_2_pin12), .pin14(n74377_2_pin9), .pin13(n74377_2_pin6),
    .pin12(n74377_2_pin5), .pin11(n74377_2_pin2));
  _74283 #(.ShowInternalStructure("true")) u_74283_2 (
    .pin1(n74283_2_pin1), .pin2(n7486_1_pin8), .pin3(n74377_2_pin15), .pin4(n74283_2_pin4),
    .pin5(n74377_2_pin12), .pin6(n7486_1_pin11), .pin7(n74283_1_pin9), .pin15(n7486_1_pin3),
    .pin14(n74377_2_pin16), .pin13(n74283_2_pin13), .pin12(n74377_2_pin19), .pin11(n7486_1_pin6),
    .pin10(n74283_2_pin10), .pin9(n74283_2_pin9));
  _74138 #(.ShowInternalStructure("true")) u_74138_2 (
    .pin1(rom_2_data[3]), .pin2(rom_2_data[4]), .pin3(rom_2_data[5]), .pin4(n74138_2_pin4),
    .pin5(n74138_2_pin4), .pin6(n74138_2_pin6), .pin7(ORI), .pin14(JMP), .pin13(IRI), .pin12(n74138_2_pin12),
    .pin11(ARI), .pin10(BRI), .pin9(MRI));  // open: pin15
  _74377 #(.ShowInternalStructure("true")) u_74377_4 (
    .pin1(ORI), .pin2(n74377_4_pin2[0]), .pin3(n74161_2_pin3), .pin4(n74161_2_pin4), .pin5(n74377_4_pin2[1]),
    .pin6(n74377_4_pin2[2]), .pin7(n74161_2_pin5), .pin8(n74161_2_pin6), .pin9(n74377_4_pin2[3]),
    .pin19(n74377_4_pin2[7]), .pin18(n74161_1_pin6), .pin17(n74161_1_pin5), .pin16(n74377_4_pin2[6]),
    .pin15(n74377_4_pin2[5]), .pin14(n74161_1_pin4), .pin13(n74161_1_pin3), .pin12(n74377_4_pin2[4]),
    .pin11(CLK));
  not not_2 (RAI, n74138_2_pin12);
  _7436 #(.ShowInternalStructure("true")) u_7436_1 (
    .pin1(n74283_2_pin4), .pin2(n74283_2_pin1), .pin3(n7436_1_pin3), .pin4(n74283_2_pin13),
    .pin5(n74283_2_pin10), .pin6(n7436_1_pin6), .pin13(n74283_1_pin4), .pin12(n74283_1_pin1),
    .pin11(n7436_1_pin11), .pin10(n74283_1_pin13), .pin9(n74283_1_pin10), .pin8(n7436_1_pin8));
  _7_Segment_Display u_7_segment_display_1 ();  // open: g, f, a, b, e, d, c, dp
  _7_Segment_Display u_7_segment_display_2 ();  // open: g, f, a, b, e, d, c, dp
  // BCD_to_7_Segment_decoder bcd_to_7_segment_decoder_1: pin names not known
  // BCD_to_7_Segment_decoder bcd_to_7_segment_decoder_2: pin names not known
  // Binary_to_BCD_converter #(.binvalue(8)) binary_to_bcd_converter_1: pin names not known
  _74377 #(.ShowInternalStructure("true")) u_74377_5 (
    .pin1(ALO), .pin2(CF), .pin3(n74283_2_pin9), .pin4(n74377_5_pin4), .pin5(ZF), .pin7(n74377_5_pin7),
    .pin8(n74377_5_pin7), .pin18(n74377_5_pin18), .pin17(n74377_5_pin18), .pin14(n74377_5_pin18),
    .pin13(n74377_5_pin18), .pin11(CLK));  // open: pin6, pin9, pin19, pin16, pin15, pin12
  _74245 #(.ShowInternalStructure("true")) u_74245_5 (
    .pin1(n74245_5_pin1), .pin2(n74161_1_pin6), .pin3(n74161_1_pin5), .pin4(n74161_1_pin4),
    .pin5(n74161_1_pin3), .pin6(n74161_2_pin6), .pin7(n74161_2_pin5), .pin8(n74161_2_pin4),
    .pin9(n74161_2_pin3), .pin19(ALO), .pin18(n74283_2_pin10), .pin17(n74283_2_pin13), .pin16(n74283_2_pin1),
    .pin15(n74283_2_pin4), .pin14(n74283_1_pin10), .pin13(n74283_1_pin13), .pin12(n74283_1_pin1),
    .pin11(n74283_1_pin4));
  _7408 #(.ShowInternalStructure("true")) u_7408_2 (
    .pin4(n7408_2_pin4), .pin5(n7408_2_pin5), .pin6(n74377_5_pin4), .pin13(n7436_1_pin11),
    .pin12(n7436_1_pin3), .pin11(n7408_2_pin4), .pin10(n7436_1_pin8), .pin9(n7436_1_pin6), .pin8(n7408_2_pin5));  // open: pin1, pin2, pin3
  _7_Segment_Display u_7_segment_display_3 ();  // open: g, f, a, b, e, d, c, dp
  // BCD_to_7_Segment_decoder bcd_to_7_segment_decoder_3: pin names not known
  // also tied to GND on the sheet: {n74161_3_pin3, n74245_3_pin1, n74138_1_pin4, n74245_4_pin1, n74138_2_pin4, n74245_5_pin1, n74377_5_pin18, n74377_5_pin7}
  // also tied to VCC on the sheet: {n74161_1_pin1, n74161_2_pin1, n74161_2_pin10, n74161_3_pin10, n74161_3_pin7, n74161_4_pin1, n74161_5_pin1, n74161_5_pin10, n74138_1_pin6, n74138_2_pin6}

  // Other names for the same wires on the sheet: FRI = ALO

  // Notes on the sheet:
  //   contents of rom_1 (hex, n*v repeats v):
  //   1e 2 1 7 7 6 0 3 1 1e 8 0 6 7
  //   Instruction-Register
  //   Memory Register
  //   Step-Counter
  //   contents of rom_2 (hex, n*v repeats v):
  //   31 53 6*5 31 53 63 5*5 31 53 6b 26 4*5 31 53 6b a6 4*5 31 53 73 1c 4*5 31 53 6*5 31 53 4b 5*5 31 53
  //   6*5 31 53 6*5 31 53 6*5 31 53 6*5 31 53 6*5 31 53 6*5 31 53 6*5 31 53 6*5 31 53 6*5 31 53 6*5 31 53
  //   6*5 31 53 6*5 31 53 6*5 31 53 6*5 31 53 6*5 31 53 6*5 31 53 6*5 31 53 6*5 31 53 6*5 31 53 6*5 31 53
  //   6*5 31 53 6*5 31 53 6*5 31 53 3c 5*5 31 53 7 5*5 31 53 6*5 31 53 63 5*5 31 53 6b 26 4*5 31 53 6b a6
  //   4*5 31 53 73 1c 4*5 31 53 6*5 31 53 4b 5*5 31 53 4b 5*5 31 53 6*5 31 53 6*5 31 53 6*5 31 53 6*5 31
  //   53 6*5 31 53 6*5 31 53 6*5 31 53 6*5 31 53 6*5 31 53 6*5 31 53 6*5 31 53 6*5 31 53 6*5 31 53 6*5 31
  //   53 6*5 31 53 6*5 31 53 6*5 31 53 6*5 31 53 6*5 31 53 6*5 31 53 6*5 31 53 6*5 31 53 3c 5*5 31 53 7
  //   5*5 31 53 6*5 31 53 63 5*5 31 53 6b 26 4*5 31 53 6b a6 4*5 31 53 73 1c 4*5 31 53 6*5 31 53 4b 5*5 31
  //   53 6*5 31 53 4b 5*5 31 53 6*5 31 53 6*5 31 53 6*5 31 53 6*5 31 53 6*5 31 53 6*5 31 53 6*5 31 53 6*5
  //   31 53 6*5 31 53 6*5 31 53 6*5 31 53 6*5 31 53 6*5 31 53 6*5 31 53 6*5 31 53 6*5 31 53 6*5 31 53 6*5
  //   31 53 6*5 31 53 6*5 31 53 6*5 31 53 3c 5*5 31 53 7 5*5 31 53 6*5 31 53 63 5*5 31 53 6b 26 4*5 31 53
  //   6b a6 4*5 31 53 73 1c 4*5 31 53 6*5 31 53 4b 5*5 31 53 4b 5*5 31 53 4b 5*5 31 53 6*5 31 53 6*5 31 53
  //   6*5 31 53 6*5 31 53 6*5 31 53 6*5 31 53 6*5 31 53 6*5 31 53 6*5 31 53 6*5 31 53 6*5 31 53 6*5 31 53
  //   6*5 31 53 6*5 31 53 6*5 31 53 6*5 31 53 6*5 31 53 6*5 31 53 6*5 31 53 6*5 31 53 6*5 31 53 3c 5*5 31
  //   53 7 5*5
  //   A-Register
  //   B-Register
  //   Program Counter
  //   Instruction Decoder
  //   ALU
  //   Control-lines
  //   Output-Register
  //   Flags-Register
endmodule
